// Logisim project Block randomizer.circ as structural Verilog: 1 circuit, main circuit main
module main (
  input  CLK,
  output [6:0] OUT_A,
  output [1:0] OUT_D
);

  wire main_2_a_b_2, main_3_a_b_2, main_4_a_b_2, main_5_a_b_2;
  wire [1:0] main_1_out, main_6_out_4, main_7_out_4, main_8_out_4, n2x2_block_1_out_4;
  wire [6:0] main_6_out_3, main_7_out_3, main_8_out_3, n2x2_block_1_out_3;

  Randomizer_main main_1 (.CLK(CLK), .OUT(main_1_out));
  _2bit_comparator_main main_2 (.in_1(2'b00), .in_2(main_1_out), .A_B_2(main_2_a_b_2));  // open: A_B, A_B_3
  _2bit_comparator_main main_3 (.in_1(2'b01), .in_2(main_1_out), .A_B_2(main_3_a_b_2));  // open: A_B, A_B_3
  _2bit_comparator_main main_4 (.in_1(2'b10), .in_2(main_1_out), .A_B_2(main_4_a_b_2));  // open: A_B, A_B_3
  _2bit_comparator_main main_5 (.in_1(2'b11), .in_2(main_1_out), .A_B_2(main_5_a_b_2));  // open: A_B, A_B_3
  _1x4_Block_main main_6 (
    .START_GEN(main_2_a_b_2), .CLK(CLK), .out_3(main_6_out_3), .out_4(main_6_out_4));  // open: out_5
  _2x2_Block u_2x2_block_1 (
    .in_1(CLK), .in_2(main_3_a_b_2), .out_3(n2x2_block_1_out_3), .out_4(n2x2_block_1_out_4));  // open: out_5
  T_Block_main main_7 (.START_GEN(main_4_a_b_2), .CLK(CLK), .out_3(main_7_out_3), .out_4(main_7_out_4));  // open: out_5
  L_Block_main main_8 (.START_GEN(main_5_a_b_2), .CLK(CLK), .out_3(main_8_out_3), .out_4(main_8_out_4));  // open: out_5
  assign OUT_A = main_2_a_b_2 ? main_6_out_3 : 7'bz;  // Controlled_Buffer controlled_buffer_1
  assign OUT_A = main_3_a_b_2 ? n2x2_block_1_out_3 : 7'bz;  // Controlled_Buffer controlled_buffer_2
  assign OUT_D = main_3_a_b_2 ? n2x2_block_1_out_4 : 2'bz;  // Controlled_Buffer controlled_buffer_3
  assign OUT_A = main_4_a_b_2 ? main_7_out_3 : 7'bz;  // Controlled_Buffer controlled_buffer_4
  assign OUT_A = main_5_a_b_2 ? main_8_out_3 : 7'bz;  // Controlled_Buffer controlled_buffer_5
  assign OUT_D = main_2_a_b_2 ? main_6_out_4 : 2'bz;  // Controlled_Buffer controlled_buffer_6
  assign OUT_D = main_4_a_b_2 ? main_7_out_4 : 2'bz;  // Controlled_Buffer controlled_buffer_7
  assign OUT_D = main_5_a_b_2 ? main_8_out_4 : 2'bz;  // Controlled_Buffer controlled_buffer_8
endmodule
