// Logisim project TEST.circ as structural Verilog: 1 circuit, main circuit main
module main (
  input  in_1,
  input  [6:0] in_2,
  input  in_3,
  input  [1:0] in_4,
  input  in_5,
  output [1:0] out_6,
  output game_over
);

  wire clock_1_out;
  wire [1:0] blc_rand_1_out_d, multiplexer_2_out;
  wire [6:0] blc_rand_1_out_a, counter_1_q, multiplexer_1_out, multiplexer_3_out;

  Clock clock_1 (.out(clock_1_out));
  BLC_RAND blc_rand_1 (
    .CLK(clock_1_out), .OUT_A(blc_rand_1_out_a), .OUT_D(blc_rand_1_out_d), .START(in_1),
    .CURRENT_GAME_ADRESS(multiplexer_3_out), .CURRENT_GAME_STATE(out_6), .GAME_OVER(game_over));  // open: OUT_B
  Multiplexer #(.width(7)) multiplexer_1 (
    .in0(in_2), .in1(blc_rand_1_out_a), .out(multiplexer_1_out), .sel(in_3));  // open: en
  Multiplexer #(.width(2)) multiplexer_2 (
    .in0(in_4), .in1(blc_rand_1_out_d), .out(multiplexer_2_out), .sel(in_3));  // open: en
  Counter #(.width(7), .max('h7f)) counter_1 (.Q(counter_1_q), .clk(clock_1_out));  // open: load, D, count, carry, clr
  Multiplexer #(.width(7)) multiplexer_3 (
    .in0(multiplexer_1_out), .in1(counter_1_q), .out(multiplexer_3_out), .sel(in_5));  // open: en
  RAM #(.addrWidth(7), .dataWidth(2), .bus("separate")) ram_1 (
    .addr(multiplexer_3_out), .din(multiplexer_2_out), .data(out_6), .clk(clock_1_out));  // open: str, sel, ld, clr
endmodule
