// Logisim project main.circ as structural Verilog: 1 circuit, main circuit main
module main (
  input  [6:0] A1,
  input  ENABLE,
  output [6:0] out_3,
  output [6:0] out_4,
  output [6:0] NOWE_A1,
  output \CZY_RUCH_BYŁ_ZABLOKOWANY ,
  output FINISH_PRZESUW,
  output FINISH_ROT
);

  wire blc_rand_1_p3, blc_rand_1_p4, blc_rand_1_p5, CLK, clock_1_out, comparator_1_eq, comparator_2_eq,
       comparator_3_eq, controlled_buffer_1_out, demultiplexer_2_out0, demultiplexer_2_out1,
       demultiplexer_3_out0, demultiplexer_3_out1, Game_CLK, gpu_manager_1_out_5, gpu_manager_1_out_6,
       gpu_manager_1_out_7, gpu_manager_1_out_8, keyboard_1_avail, main_1_finish, main_1_ram_clk,
       main_1_zderzenie, main_2_ram_clk, main_2_zd, main_3_ram_clk, main_3_zd, main_4_flaga, main_4_flaga_2,
       main_4_trwajaca_akcja, or_1_out, RAM_CLK;
  wire [1:0] Data_In, Data_Out, demultiplexer_1_p3, Game_Data, Game_Data_In, Gpu_Data, main_1_data_out,
       main_2_data_out, main_3_data_out;
  wire [2:0] State_Select;
  wire [6:0] Adress, Game_Adress, GPU_Adress, gpu_manager_1_out_4, keyboard_1_data, main_1_a, main_2_a,
       main_3_a, multiplier_1_out;
  wire [7:0] gpu_1_p5, gpu_1_p6, gpu_1_p7, gpu_1_p8, gpu_1_p9, gpu_1_p10, gpu_1_p11, gpu_1_p12, gpu_1_p13,
       gpu_1_p14, gpu_1_p15, gpu_1_p16, gpu_1_p17, gpu_1_p18, gpu_1_p19, gpu_1_p20;

  // Demultiplexer #(.select(3), .width(2)) demultiplexer_1: pin names not known; wires that end beside it: Data_Out, State_Select, demultiplexer_1_p3, Game_Data, Gpu_Data
  Counter #(.width(4), .max('hf)) counter_1 (.Q(out_4[3:0]), .clk(main_1_finish));  // open: load, D, count, carry, clr
  Adder #(.width(7)) adder_1 (.a(7'b0000010), .b(multiplier_1_out), .out(out_3));  // open: cin, cout
  Multiplier #(.width(7)) multiplier_1 (
    .a(7'b0001000), .b({3'b000, out_4[3:0]}), .out(multiplier_1_out));  // open: cin, cout
  Clock clock_1 (.out(clock_1_out));
  Comparator #(.width(3)) comparator_1 (.a(State_Select), .b(3'b000), .eq(comparator_1_eq));  // open: gt, lt
  Comparator #(.width(3)) comparator_2 (.a(State_Select), .b(3'b001), .eq(comparator_2_eq));  // open: gt, lt
  Demultiplexer demultiplexer_2 (
    .out0(demultiplexer_2_out0), .out1(demultiplexer_2_out1), .in(clock_1_out), .sel(main_4_trwajaca_akcja));  // open: en
  Demultiplexer demultiplexer_3 (
    .out0(demultiplexer_3_out0), .out1(demultiplexer_3_out1), .in(ENABLE), .sel(main_4_trwajaca_akcja));  // open: en
  opadanie_main main_1 (
    .A1(out_3), .DATA_IN(demultiplexer_1_p3), .CLK(CLK), .ENABLE(comparator_2_eq),
    .DATA_OUT(main_1_data_out), .A(main_1_a), .RAM_CLK(main_1_ram_clk), .FINISH(main_1_finish),
    .ZDERZENIE(main_1_zderzenie));
  Multiplexer #(.width(7)) multiplexer_1 (
    .in0(main_3_a), .in1(main_2_a), .out(Game_Adress), .sel(main_4_trwajaca_akcja));  // open: en
  // BLC_RAND blc_rand_1: pin names not known; wires that end beside it: comparator_1_eq, CLK, blc_rand_1_p3, blc_rand_1_p4, blc_rand_1_p5
  przesuwanie_main main_2 (
    .A1(A1), .CLK(demultiplexer_2_out1), .ENABLE(demultiplexer_3_out1), .DATA_IN(Game_Data),
    .FLAGA(main_4_flaga), .NOWE_A1(NOWE_A1), .DATA_OUT(main_2_data_out), .RAM_CLK(main_2_ram_clk),
    .ZD(main_2_zd), .A(main_2_a), .FINISH(FINISH_PRZESUW));
  rotacja_main main_3 (
    .A1(A1), .CLK(demultiplexer_2_out0), .ENABLE(demultiplexer_3_out0), .DATA_IN(Game_Data),
    .FLAGA(main_4_flaga_2), .DATA_OUT(main_3_data_out), .RAM_CLK(main_3_ram_clk), .ZD(main_3_zd),
    .A(main_3_a), .FINISH(FINISH_ROT));
  Multiplexer #(.select(3), .width(7)) multiplexer_2 (
    .out(Adress), .sel(State_Select));  // open: in0, in1, in2, in3, in4, in5, in6, in7, en
  Multiplexer #(.select(3), .width(2)) multiplexer_3 (
    .out(Data_In), .sel(State_Select));  // open: in0, in1, in2, in3, in4, in5, in6, in7, en
  // Multiplexer #(.select(3)) multiplexer_4: pin names not known; wires that end beside it: CLK, main_1_ram_clk, 1'b0, State_Select, RAM_CLK
  Multiplexer multiplexer_5 (
    .in0(main_3_ram_clk), .in1(main_2_ram_clk), .out(Game_CLK), .sel(main_4_trwajaca_akcja));  // open: en
  Multiplexer #(.width(2)) multiplexer_6 (
    .in0(main_3_data_out), .in1(main_2_data_out), .out(Game_Data_In), .sel(main_4_trwajaca_akcja));  // open: en
  Keyboard keyboard_1 (.clk(clock_1_out), .avail(keyboard_1_avail), .data(keyboard_1_data));  // open: re, clr
  Clock clock_2 (.out(CLK));
  State_Selector state_selector_1 (
    .Keyboard__Input_Happened(keyboard_1_avail), .out_7(State_Select), .New_Block_Request(main_1_zderzenie),
    .Generating_Ended(blc_rand_1_p3), .Shifting_Down_Ended(main_1_finish), .Player_Input_Ended(or_1_out),
    .Render(gpu_manager_1_out_8));
  Multiplexer multiplexer_7 (
    .in0(main_3_zd), .in1(main_2_zd), .out(\CZY_RUCH_BYŁ_ZABLOKOWANY ), .sel(main_4_trwajaca_akcja));  // open: en
  or or_1 (or_1_out, FINISH_ROT, FINISH_PRZESUW);
  koder_klawiatura_main main_4 (
    .wejscie_ASCI(keyboard_1_data), .CLK(keyboard_1_avail), .RESET(FINISH_PRZESUW), .FLAGA(main_4_flaga),
    .FLAGA_2(main_4_flaga_2), .RESET_2(FINISH_ROT), .TRWAJACA_AKCJA(main_4_trwajaca_akcja));
  RAM #(.addrWidth(7), .dataWidth(2), .bus("separate")) ram_1 (
    .addr(Adress), .din(Data_In), .data(Data_Out), .clk(RAM_CLK));  // open: str, sel, ld, clr
  assign controlled_buffer_1_out = comparator_3_eq ? CLK : 1'bz;  // Controlled_Buffer controlled_buffer_1
  Comparator #(.width(3)) comparator_3 (.a(State_Select), .b(3'b010), .eq(comparator_3_eq));  // open: gt, lt
  GPU_manager gpu_manager_1 (
    .in_1(Gpu_Data), .in_2(controlled_buffer_1_out), .out_3(GPU_Adress), .out_4(gpu_manager_1_out_4),
    .out_5(gpu_manager_1_out_5), .out_6(gpu_manager_1_out_6), .out_7(gpu_manager_1_out_7),
    .out_8(gpu_manager_1_out_8));
  Pull_Resistor pull_resistor_1 (.node(controlled_buffer_1_out));
  // GPU gpu_1: pin names not known; wires that end beside it: gpu_manager_1_out_4, gpu_manager_1_out_5, gpu_manager_1_out_6, gpu_manager_1_out_7, gpu_1_p5, gpu_1_p6, gpu_1_p7, gpu_1_p8, gpu_1_p9, gpu_1_p10, gpu_1_p11, gpu_1_p12, gpu_1_p13, gpu_1_p14, gpu_1_p15, gpu_1_p16, gpu_1_p17, gpu_1_p18, gpu_1_p19, gpu_1_p20
  DotMatrix #(.inputtype("row"), .matrixcols(8), .matrixrows(16), .dotshape("circle")) dotmatrix_1 (
    .row0(gpu_1_p5), .row1(gpu_1_p6), .row2(gpu_1_p7), .row3(gpu_1_p8), .row4(gpu_1_p9), .row5(gpu_1_p10),
    .row6(gpu_1_p11), .row7(gpu_1_p12), .row8(gpu_1_p13), .row9(gpu_1_p14), .row10(gpu_1_p15),
    .row11(gpu_1_p16), .row12(gpu_1_p17), .row13(gpu_1_p18), .row14(gpu_1_p19), .row15(gpu_1_p20));

  assign out_4[6:4] = 3'b000;

  // Notes on the sheet:
  //   ten finisz wystepuje ale od razu sie gasi, bo resetuje tez koder i zmienia flage akcji
endmodule
