// Logisim project GPU.circ as structural Verilog: 1 circuit, main circuit GPU
module GPU (
  input  [6:0] in_1,
  input  in_2,
  input  in_3,
  input  in_4,
  output [7:0] out_5,
  output [7:0] out_6,
  output [7:0] out_7,
  output [7:0] out_8,
  output [7:0] out_9,
  output [7:0] out_10,
  output [7:0] out_11,
  output [7:0] out_12,
  output [7:0] out_13,
  output [7:0] out_14,
  output [7:0] out_15,
  output [7:0] out_16,
  output [7:0] out_17,
  output [7:0] out_18,
  output [7:0] out_19,
  output [7:0] out_20
);

  wire [6:0] divider_1_out, divider_1_rem;
  wire [7:0] demultiplexer_1_out7, demultiplexer_2_out0, demultiplexer_2_out1, demultiplexer_2_out2,
       demultiplexer_2_out3, demultiplexer_2_out4, demultiplexer_2_out5, demultiplexer_2_out6,
       demultiplexer_2_out7, demultiplexer_2_out8, demultiplexer_2_out9, demultiplexer_2_out10,
       demultiplexer_2_out11, demultiplexer_2_out12, demultiplexer_2_out13, demultiplexer_2_out14,
       demultiplexer_2_out15;

  Divider #(.width(7)) divider_1 (.a(in_1), .b(7'b0001000), .out(divider_1_out), .rem(divider_1_rem));  // open: upper
  Demultiplexer #(.select(3)) demultiplexer_1 (
    .out0(demultiplexer_1_out7[7]), .out1(demultiplexer_1_out7[6]), .out2(demultiplexer_1_out7[5]),
    .out3(demultiplexer_1_out7[4]), .out4(demultiplexer_1_out7[3]), .out5(demultiplexer_1_out7[2]),
    .out6(demultiplexer_1_out7[1]), .out7(demultiplexer_1_out7[0]), .in(1'b1), .sel(divider_1_rem[2:0]));  // open: en
  Demultiplexer #(.select(4), .width(8)) demultiplexer_2 (
    .out0(demultiplexer_2_out0), .out1(demultiplexer_2_out1), .out2(demultiplexer_2_out2),
    .out3(demultiplexer_2_out3), .out4(demultiplexer_2_out4), .out5(demultiplexer_2_out5),
    .out6(demultiplexer_2_out6), .out7(demultiplexer_2_out7), .out8(demultiplexer_2_out8),
    .out9(demultiplexer_2_out9), .out10(demultiplexer_2_out10), .out11(demultiplexer_2_out11),
    .out12(demultiplexer_2_out12), .out13(demultiplexer_2_out13), .out14(demultiplexer_2_out14),
    .out15(demultiplexer_2_out15), .in(demultiplexer_1_out7), .sel(divider_1_out[3:0]));  // open: en
  _8IO_Buffer u_8io_buffer_1 (
    .in_1(demultiplexer_2_out8), .in_2(demultiplexer_2_out9), .in_3(demultiplexer_2_out10),
    .in_4(demultiplexer_2_out11), .in_5(demultiplexer_2_out12), .in_6(demultiplexer_2_out13),
    .in_7(demultiplexer_2_out14), .in_8(demultiplexer_2_out15), .out_12(out_13), .out_13(out_14),
    .out_14(out_15), .out_15(out_16), .out_16(out_17), .out_17(out_18), .out_18(out_19), .out_19(out_20),
    .in_9(in_2), .in_10(in_3), .in_11(in_4));
  _8IO_Buffer u_8io_buffer_2 (
    .in_1(demultiplexer_2_out0), .in_2(demultiplexer_2_out1), .in_3(demultiplexer_2_out2),
    .in_4(demultiplexer_2_out3), .in_5(demultiplexer_2_out4), .in_6(demultiplexer_2_out5),
    .in_7(demultiplexer_2_out6), .in_8(demultiplexer_2_out7), .out_12(out_5), .out_13(out_6), .out_14(out_7),
    .out_15(out_8), .out_16(out_9), .out_17(out_10), .out_18(out_11), .out_19(out_12), .in_9(in_2),
    .in_10(in_3), .in_11(in_4));
endmodule
