// Logisim project keyboardmanager.circ as structural Verilog: 1 circuit, main circuit Keyboard Manager
module Keyboard_Manager (
  input  [6:0] in_1,
  input  in_2,
  input  in_3,
  output [6:0] out_4,
  output out_5,
  output out_6
);

  wire comparator_1_eq, comparator_2_eq, comparator_3_eq, comparator_4_eq, or_1_out;

  Comparator #(.width(7)) comparator_1 (.a(7'b1110001), .b(in_1), .eq(comparator_1_eq));  // open: gt, lt
  Comparator #(.width(7)) comparator_2 (.a(in_1), .b(7'b1100101), .eq(comparator_2_eq));  // open: gt, lt
  Comparator #(.width(7)) comparator_3 (.a(7'b1100001), .b(in_1), .eq(comparator_3_eq));  // open: gt, lt
  Comparator #(.width(7)) comparator_4 (.a(in_1), .b(7'b1100100), .eq(comparator_4_eq));  // open: gt, lt
  or or_1 (or_1_out, comparator_1_eq, comparator_2_eq, comparator_3_eq, comparator_4_eq);
  Register #(.width(7)) register_1 (.D(in_1), .Q(out_4), .clk(or_1_out));  // open: en, clr
  D_Flip_Flop d_ff_1 (.clk(or_1_out), .D(1'b1), .Q(out_6), .reset(in_3));  // open: Qn, preset, en

  assign out_5 = in_2;
endmodule
